# Fritzing sketch Experimento_1_Amplificador_Inversor (saved by Fritzing 0.9.3b)
breadboards: 1

parts:
  U1 = LM 358 Dual Op-Amp [package="DIP8 [THT]"]
  R1 = Resistor [tolerance=±5% resistance=1k package="0805 [SMD]"]
  R2 = Resistor [tolerance=±5% resistance=2.2k package="0805 [SMD]"]

nets:
  N1: U1.connector0, R2.Pin_0
  N2: U1.connector1, R1.Pin_0, R2.Pin_1

notes:
  -12 Volts
  +12 Volts
  Onda Senoidal, Serra, Quadrada, etc
  GNG do Gerador de Funçoes
  Multimeter Positive Probe
  Multimeter Negative Probe
  Experimento I - Amplificador Inversor
  LM358P
  COM da Fonte Simétrica
  Gerador de Funcoes
