# Fritzing sketch Experimento_2_A_Filtro_Butterworth_Passa_Alta (saved by Fritzing 0.9.3b)
breadboards: 1

parts:
  U1 = LM 358 Dual Op-Amp [package="DIP8 [THT]"]
  R1 = Resistor [tolerance=±5% resistance=10k package="0805 [SMD]"]
  R2 = Resistor [tolerance=±5% resistance=12k package="0805 [SMD]"]
  C1 = Capacitor [part_number="473 (47nF)" package=cap-pth-small2]
  C2 = Capacitor [part_number="473 (47nF)" package=cap-pth-small2]
  R3 = Resistor [tolerance=±5% resistance=18k package="0805 [SMD]"]
  R4 = Resistor [tolerance=±5% resistance=18k package="0805 [SMD]"]

nets:
  N1: U1.connector0, R2.Pin_0, R4.Pin_1
  N2: U1.connector1, R1.Pin_0, R2.Pin_1
  N3: U1.connector2, C1.1, R3.Pin_0
  N4: C1.2, C2.1, C2.2, R3.Pin_1, R4.Pin_0

notes:
  -12 Volts
  +12 Volts
  Onda Senoidal, Serra, Quadrada, etc
  GNG do Gerador de Funçoes
  Multimeter Positive Probe
  Multimeter Negative Probe
  Experimento II - Filtro de Butterworth
  LM358P
  COM da Fonte Simétrica
  Gerador de Funcoes
  Projeto de um Filtro Passa Altas
